# Fritzing sketch FYDP - Full Schematic (saved by Fritzing 0.9.2b)
stripboards: 1
perfboards: 1

parts:
  Arduino_Uno = Arduino Uno (Rev3)
  PG27_Planetary_Gearbox_with_RS775_Motor = DC Motor
  12V = LIPO-2000mAh [package=lipo-2000]
  R1 = Resistor [tolerance=±5% resistance=10k package=THT]
  12V_/_30A_Relay = RELAY [package=relay-g5q]
  E-Stop_Light = LED - 3mm [color="Red (633nm)" package="3 mm [THT]"]
  R2 = Resistor [tolerance=±5% resistance=180 package=THT]
  R3 = Resistor [tolerance=±5% resistance=220 package=THT]
  Rectifier_Diode = Rectifier Diode [part_number=1N4004 package="Melf DO-213 AB [SMD]"]
  30A_Fuse = FUSE [package=fuse_5mm]
  R4 = Resistor [tolerance=±5% resistance=220 package=THT]
  Zener_Diode = Zener Diode [part_number=1N4732A breakdown_voltage=9.1V package="Melf DO-213 AB [SMD]"]
  Transistor = NPN-Transistor [part_number=TIP102 package="TO92 [THT]"]
  Low_Battery_Light = LED - 3mm [color="Yellow (585nm)" package="3 mm [THT]"]
  Power/Ready_Light = LED - 3mm [color="Green (555nm)" package="3 mm [THT]"]
  Encoder_(am-2923) = Header 4 [package=screwterminal-3.5mm-4_lock]
  MyoWare_Muscle_Sensor_(EMG1) = Header 3 [package=screwterminal-3.5mm-3_lock.007s]
  MyoWare_Muscle_Sensor_(EMG2) = Header 3 [package=screwterminal-3.5mm-3_lock.007s]
  Mega_Motor_Shield = Monster Moto Shield [part_number=RB-Rop-01]
  E-Stop_Switch = SPST Switch [package=switch-spdt]
  Power_Switch = SWITCH-SPST-2 [package=switch-spst-vertical]
  S2 = Round Pushbutton  # not connected
  R5 = Resistor [tolerance=±5% resistance=10k package=THT]
  12V_-_9V_Voltage_Regulator = V_REG_NCP50X [package=dpak-5]

nets (from the schematic view):
  N1: Arduino_Uno.A0, MyoWare_Muscle_Sensor_(EMG1).1
  N2: Arduino_Uno.A1, MyoWare_Muscle_Sensor_(EMG2).1
  N3: Arduino_Uno.D8, Mega_Motor_Shield.INB1_-_D8
  N4: Arduino_Uno.D9_PWM, Encoder_(am-2923).3
  N5: Arduino_Uno.D10_PWM/SS, Encoder_(am-2923).4
  N6: Arduino_Uno.D2, Power/Ready_Light.anode, E-Stop_Switch.O, R5.Pin_1
  N7: Arduino_Uno.D3_PWM, E-Stop_Light.anode
  N8: Arduino_Uno.D5_PWM, Mega_Motor_Shield.PWM1_-_D5
  N9: Arduino_Uno.D6_PWM, Mega_Motor_Shield.PWM2_-_D6
  N10: Arduino_Uno.5V, E-Stop_Switch.P
  GND: Arduino_Uno.GND, 12V.-, Low_Battery_Light.cathode, MyoWare_Muscle_Sensor_(EMG1).3, MyoWare_Muscle_Sensor_(EMG2).3, Mega_Motor_Shield.GND, Mega_Motor_Shield.GND_-_GND@0, Mega_Motor_Shield.GND_-_GND@2, 12V_-_9V_Voltage_Regulator.GND
  N11: Arduino_Uno.VIN, Power_Switch.O
  N12: PG27_Planetary_Gearbox_with_RS775_Motor.pin_1, PG27_Planetary_Gearbox_with_RS775_Motor.pin_2, Mega_Motor_Shield.OUTA1, Mega_Motor_Shield.OUTB1
  N13: 12V.+, 30A_Fuse.1
  N14: R1.Pin_0, E-Stop_Switch.S
  N15: R1.Pin_1, R3.Pin_1, R4.Pin_1, Transistor.E, Encoder_(am-2923).2
  N16: 12V_/_30A_Relay.COIL2, R2.Pin_0, Rectifier_Diode.cathode
  N17: 12V_/_30A_Relay.MAIN, Mega_Motor_Shield.VCC
  N18: 12V_/_30A_Relay.NO, 30A_Fuse.2, 12V_-_9V_Voltage_Regulator.IN
  N19: 12V_/_30A_Relay.COIL1, Rectifier_Diode.anode, Transistor.C
  N20: E-Stop_Light.cathode, R3.Pin_0
  N21: R2.Pin_1, Zener_Diode.cathode
  N22: R4.Pin_0, Power/Ready_Light.cathode
  N23: Zener_Diode.anode, Low_Battery_Light.anode
  N24: Transistor.B, R5.Pin_0
  N25: Encoder_(am-2923).1, MyoWare_Muscle_Sensor_(EMG1).2
  N26: Power_Switch.P, 12V_-_9V_Voltage_Regulator.OUT
